# Fritzing sketch Исходний принципиальной схемы (saved by Fritzing 0.9.10b)

parts:
  Компонент1 = BME280 Breakout
  C1 = Ceramic Capacitor [capacitance="100 nF" voltage=35V package="1206 [SMD, multilayer]"]  # not connected
  Mod1 = TP4056 [part_number=TP4056]
  WeMos_D1_Mini1 = WeMos D1 Mini
  BAT1 = Battery Holders [package=lipo-1100mAh]
  A1 = LoRa sx1278 module [package=THT]

nets:
  N1: Компонент1.SDI/SDA, WeMos_D1_Mini1.D7
  N2: Компонент1.SCK/SCL, WeMos_D1_Mini1.D8
  3.3V: Компонент1.3.3V, WeMos_D1_Mini1.3V3
  N3: Компонент1.GND, Mod1.pin6, WeMos_D1_Mini1.G, A1.Pin_1, A1.Pin_12, A1.Pin_15
  N4: Mod1.pin3, BAT1.+
  N5: Mod1.pin4, WeMos_D1_Mini1.5V, A1.Pin_5
  N6: Mod1.pin5, BAT1.-
  N7: WeMos_D1_Mini1.D1, A1.Pin_2
  N8: WeMos_D1_Mini1.D2, A1.Pin_3
  N9: WeMos_D1_Mini1.D3, A1.Pin_4
  N10: WeMos_D1_Mini1.D4, A1.Pin_6

notes:
  Li-Po 11.1v 1100mAh - Осуществляет питание устройств
  BME280 - Измеряет температуру во время запуска устройства
  TP4056 - Выступает в роли стабилизации питания от аккумулятора. CC - выполняет роль блокировочного конденстора
  SX1278 (RA-02) - выполняет роль отправки и получения данных устройства
  WEMOS D1 MINI - Отладочная плата для отправки/передачи данных с датчиков

custom parts:
  TP4056: TP4056 Lithium battery charger / protection module. (this one has the pins on .1 boundaried unlike the original)
  LoRa sx1278 module: SX1278 Long Range RF Wireless Power Mental Module.
